// Digital circuit Digital_Simulation_01-04.dig as structural Verilog
module Digital_Simulation_01_04 (
  input  C1,
  input  C2,
  output Z
);

  and and_1 (Z, C1, C2);

  // Notes on the sheet:
  //   C1: Hz: 10
endmodule
