// Digital circuit Digital_Simulation_02-02.dig as structural Verilog
module Digital_Simulation_02_02 (
  input  A,
  input  B,
  output Output
);

  wire and_1_out, not_1_out, not_2_out, or_1_out, or_2_out;

  not not_1 (not_1_out, B);
  or or_1 (or_1_out, not_2_out, B);
  not not_2 (not_2_out, A);
  or or_2 (or_2_out, not_1_out, A);
  and and_1 (and_1_out, or_1_out, or_2_out);
  not not_3 (Output, and_1_out);
endmodule
