// Digital circuit Digital_Simulation_02-03.dig as structural Verilog
module Digital_Simulation_02_03 (
  input  A,
  input  B,
  input  Cin,
  output Sum,
  output Cout
);

  wire not_1_out, not_2_out, not_3_out, or_1_out, or_2_out, or_3_out, or_4_out, or_5_out, or_6_out, or_7_out;

  not not_1 (not_1_out, A);
  not not_2 (not_2_out, B);
  not not_3 (not_3_out, Cin);
  or or_1 (or_1_out, not_1_out, not_2_out, Cin);
  or or_2 (or_2_out, not_1_out, B, not_3_out);
  or or_3 (or_3_out, A, not_2_out, not_3_out);
  or or_4 (or_4_out, A, B, Cin);
  or or_5 (or_5_out, not_1_out, B, Cin);
  or or_6 (or_6_out, A, not_2_out, Cin);
  or or_7 (or_7_out, A, B);
  and and_1 (Cout, or_5_out, or_6_out, or_7_out);
  and and_2 (Sum, or_1_out, or_2_out, or_3_out, or_4_out);
endmodule
