// Digital circuit Digital_Simulation_02-05.dig as structural Verilog
module Digital_Simulation_02_05 (
  input  A,
  input  C,
  input  B,
  input  D,
  output Z1,
  output Z2,
  output Z3
);

  wire and_1_out, and_2_out, and_3_out, and_4_out, and_7_out, and_8_out, and_9_out, and_10_out, and_11_out,
       and_12_out, and_13_out, N1, N2, nor_1_out, nor_2_out, nor_3_out, nor_4_out, not_1_out, not_2_out,
       not_3_out, not_4_out, not_5_out, not_6_out, or_1_out, or_4_out;

  not not_1 (not_1_out, D);
  not not_2 (not_2_out, B);
  not not_3 (not_3_out, D);
  not not_4 (not_4_out, B);
  not not_5 (not_5_out, C);
  not not_6 (not_6_out, A);
  and and_1 (and_1_out, B, not_1_out);
  and and_2 (and_2_out, not_2_out, D);
  and and_3 (and_3_out, B, not_3_out);
  and and_4 (and_4_out, not_4_out, D);
  nor nor_1 (nor_1_out, B, N2, D, N1);
  nor nor_2 (nor_2_out, N1, N2);
  and and_5 (N1, A, not_5_out);
  and and_6 (N2, not_6_out, C);
  and and_7 (and_7_out, and_1_out, N1);
  and and_8 (and_8_out, N1, and_2_out);
  and and_9 (and_9_out, B, D, nor_2_out);
  nor nor_3 (nor_3_out, N1, N2);
  nor nor_4 (nor_4_out, N1, N2);
  and and_10 (and_10_out, N2, and_4_out);
  or or_1 (or_1_out, and_7_out, N1, and_8_out);
  and and_11 (and_11_out, and_3_out, N2);
  or or_2 (Z3, nor_1_out, and_9_out);
  and and_12 (and_12_out, nor_3_out, and_1_out);
  and and_13 (and_13_out, nor_4_out, and_4_out);
  or or_3 (Z1, and_12_out, or_1_out);
  or or_4 (or_4_out, and_11_out, N2, and_10_out);
  or or_5 (Z2, and_13_out, or_4_out);

  // Other names for the same wires on the sheet: B1 = B; D1 = D
endmodule
