// Digital circuit Digital_Simulation_02-09.dig as structural Verilog
module Digital_Simulation_02_09 (
  input  S0,
  input  S1,
  input  X0,
  input  X1,
  input  X2,
  input  X3,
  output Z
);

  wire and_1_out, and_2_out, and_3_out, and_4_out, and_5_out, nor_1_out, nor_2_out, nor_3_out, not_1_out,
       not_2_out;

  not not_1 (not_1_out, S0);
  not not_2 (not_2_out, S1);
  nor nor_1 (nor_1_out, S0, S1);
  nor nor_2 (nor_2_out, not_1_out, S1);
  nor nor_3 (nor_3_out, S0, not_2_out);
  and and_1 (and_1_out, S0, S1);
  and and_2 (and_2_out, nor_1_out, X0);
  and and_3 (and_3_out, nor_2_out, X1);
  and and_4 (and_4_out, nor_3_out, X2);
  and and_5 (and_5_out, and_1_out, X3);
  or or_1 (Z, and_2_out, and_3_out, and_4_out, and_5_out);
endmodule
