// Digital circuit Digital_Simulation_03-02.dig as structural Verilog
module Digital_Simulation_03_02 (
  input  [2:0] In,
  output [7:0] Z
);

  wire not_1_out, not_2_out, not_3_out;
  wire [6:6] and_1_out, and_2_out, and_3_out, and_4_out, and_5_out, and_6_out, and_7_out, and_8_out;
  wire [7:0] or_1_out, or_2_out;

  not not_1 (not_1_out, In[2]);
  not not_2 (not_2_out, In[1]);
  not not_3 (not_3_out, In[0]);
  and and_1 (and_1_out[6], not_3_out, not_2_out, not_1_out);
  and and_2 (and_2_out[6], In[0], not_2_out, not_1_out);
  and and_3 (and_3_out[6], not_3_out, In[1], not_1_out);
  and and_4 (and_4_out[6], In[0], In[1], not_1_out);
  and and_5 (and_5_out[6], not_3_out, not_2_out, In[2]);
  and and_6 (and_6_out[6], In[0], not_2_out, In[2]);
  and and_7 (and_7_out[6], not_3_out, In[1], In[2]);
  and and_8 (and_8_out[6], In[0], In[1], In[2]);
  assign or_1_out = {1'b0, and_1_out[6], 3'b000, and_1_out[6], 2'b00} | {1'b0, {2{and_2_out[6]}}, 1'b0, and_2_out[6], 2'b00, and_2_out[6]} | {1'b0, {2{and_3_out[6]}}, 2'b00, {3{and_3_out[6]}}} | {1'b0, and_4_out[6], 2'b00, {2{and_4_out[6]}}, 2'b00};  // Or or_1, 8 bits wide
  assign or_2_out = {1'b0, {2{and_5_out[6]}}, 1'b0, {4{and_5_out[6]}}} | {1'b0, and_6_out[6], 2'b00, {2{and_6_out[6]}}, 2'b00} | {1'b0, {2{and_7_out[6]}}, 4'b0000, and_7_out[6]} | {1'b0, {2{and_8_out[6]}}, 3'b000, and_8_out[6], 1'b0};  // Or or_2, 8 bits wide
  assign Z = or_1_out | or_2_out;  // Or or_3, 8 bits wide

  // Other names for the same wires on the sheet: a = In[0]; b = In[1]; c = In[2]
endmodule
