// Digital circuit Digital_Simulation_03-03.dig as structural Verilog
module Digital_Simulation_03_03 (
  input  [3:0] In,
  input  [1:0] Selector,
  output [3:0] Output
);

  wire _0, _1, _2, _2_4_2_1_code, _3, _4, _5, _6, _6_4_2__3_code, _7, _8, _9, Cyclic, Excess_3, not_1_out,
       not_2_out, not_3_out, not_4_out, not_5_out, not_6_out;
  wire [0:0] and_25_out, and_34_out;
  wire [1:1] and_15_out, and_26_out, and_27_out, and_35_out, and_36_out, and_44_out;
  wire [2:2] and_16_out, and_17_out, and_18_out, and_19_out, and_28_out, and_29_out, and_30_out, and_31_out,
       and_37_out, and_43_out, and_46_out, and_48_out;
  wire [3:0] or_1_out, or_2_out, or_3_out, or_4_out, or_5_out, or_6_out, or_7_out, or_8_out, or_9_out,
       or_10_out, or_11_out, or_12_out;
  wire [3:3] and_20_out, and_21_out, and_22_out, and_23_out, and_24_out, and_32_out, and_33_out, and_38_out,
       and_39_out, and_40_out, and_41_out, and_42_out, and_45_out, and_47_out, and_49_out, and_50_out,
       and_51_out;

  not not_1 (not_1_out, In[3]);
  not not_2 (not_2_out, In[2]);
  not not_3 (not_3_out, In[1]);
  not not_4 (not_4_out, Selector[1]);
  not not_5 (not_5_out, Selector[0]);
  not not_6 (not_6_out, In[0]);
  and and_1 (Excess_3, not_5_out, not_4_out);
  and and_2 (Cyclic, Selector[0], not_4_out);
  and and_3 (_2_4_2_1_code, not_5_out, Selector[1]);
  and and_4 (_6_4_2__3_code, Selector[0], Selector[1]);
  and and_5 (_0, not_6_out, not_3_out, not_2_out, not_1_out);
  and and_6 (_1, In[0], not_3_out, not_2_out, not_1_out);
  and and_7 (_2, not_6_out, In[1], not_2_out, not_1_out);
  and and_8 (_3, In[0], In[1], not_2_out, not_1_out);
  and and_9 (_4, not_6_out, not_3_out, In[2], not_1_out);
  and and_10 (_5, In[0], not_3_out, In[2], not_1_out);
  and and_11 (_6, not_6_out, In[1], In[2], not_1_out);
  and and_12 (_7, In[0], In[1], In[2], not_1_out);
  and and_13 (_8, not_6_out, not_3_out, not_2_out, In[3]);
  and and_14 (_9, In[0], not_3_out, not_2_out, In[3]);
  and and_15 (and_15_out[1], Excess_3, _0);
  and and_16 (and_16_out[2], Excess_3, _1);
  and and_17 (and_17_out[2], Excess_3, _2);
  and and_18 (and_18_out[2], Excess_3, _3);
  and and_19 (and_19_out[2], Excess_3, _4);
  and and_20 (and_20_out[3], Excess_3, _5);
  and and_21 (and_21_out[3], Excess_3, _6);
  and and_22 (and_22_out[3], Excess_3, _7);
  and and_23 (and_23_out[3], Excess_3, _8);
  and and_24 (and_24_out[3], Excess_3, _9);
  and and_25 (and_25_out[0], Cyclic, _1);
  and and_26 (and_26_out[1], Cyclic, _2);
  and and_27 (and_27_out[1], Cyclic, _3);
  and and_28 (and_28_out[2], Cyclic, _4);
  and and_29 (and_29_out[2], Cyclic, _5);
  and and_30 (and_30_out[2], Cyclic, _6);
  and and_31 (and_31_out[2], Cyclic, _7);
  and and_32 (and_32_out[3], Cyclic, _8);
  and and_33 (and_33_out[3], Cyclic, _9);
  and and_34 (and_34_out[0], _2_4_2_1_code, _1);
  and and_35 (and_35_out[1], _2_4_2_1_code, _2);
  and and_36 (and_36_out[1], _2_4_2_1_code, _3);
  and and_37 (and_37_out[2], _2_4_2_1_code, _4);
  and and_38 (and_38_out[3], _2_4_2_1_code, _5);
  and and_39 (and_39_out[3], _2_4_2_1_code, _6);
  and and_40 (and_40_out[3], _2_4_2_1_code, _7);
  and and_41 (and_41_out[3], _2_4_2_1_code, _8);
  and and_42 (and_42_out[3], _2_4_2_1_code, _9);
  and and_43 (and_43_out[2], _6_4_2__3_code, _1);
  and and_44 (and_44_out[1], _6_4_2__3_code, _2);
  and and_45 (and_45_out[3], _6_4_2__3_code, _3);
  and and_46 (and_46_out[2], _6_4_2__3_code, _4);
  and and_47 (and_47_out[3], _6_4_2__3_code, _5);
  and and_48 (and_48_out[2], _6_4_2__3_code, _6);
  and and_49 (and_49_out[3], _6_4_2__3_code, _7);
  and and_50 (and_50_out[3], _6_4_2__3_code, _8);
  and and_51 (and_51_out[3], _6_4_2__3_code, _9);
  assign or_1_out = {2'b00, {2{and_15_out[1]}}} | {1'b0, and_16_out[2], 2'b00} | {1'b0, and_17_out[2], 1'b0, and_17_out[2]} | {1'b0, {2{and_18_out[2]}}, 1'b0} | {1'b0, {3{and_19_out[2]}}};  // Or or_1, 4 bits wide
  assign or_2_out = {and_20_out[3], 3'b000} | {and_21_out[3], 2'b00, and_21_out[3]} | {and_22_out[3], 1'b0, and_22_out[3], 1'b0} | {and_23_out[3], 1'b0, {2{and_23_out[3]}}} | {{2{and_24_out[3]}}, 2'b00};  // Or or_2, 4 bits wide
  assign or_3_out = 4'b0000 | {3'b000, and_25_out[0]} | {2'b00, {2{and_26_out[1]}}} | {2'b00, and_27_out[1], 1'b0} | {1'b0, {2{and_28_out[2]}}, 1'b0};  // Or or_3, 4 bits wide
  assign or_4_out = {1'b0, {3{and_29_out[2]}}} | {1'b0, and_30_out[2], 1'b0, and_30_out[2]} | {1'b0, and_31_out[2], 2'b00} | {{2{and_32_out[3]}}, 2'b00} | {{2{and_33_out[3]}}, 1'b0, and_33_out[3]};  // Or or_4, 4 bits wide
  assign or_5_out = 4'b0000 | {3'b000, and_34_out[0]} | {2'b00, and_35_out[1], 1'b0} | {2'b00, {2{and_36_out[1]}}} | {1'b0, and_37_out[2], 2'b00};  // Or or_5, 4 bits wide
  assign or_6_out = {and_38_out[3], 1'b0, {2{and_38_out[3]}}} | {{2{and_39_out[3]}}, 2'b00} | {{2{and_40_out[3]}}, 1'b0, and_40_out[3]} | {{3{and_41_out[3]}}, 1'b0} | {4{and_42_out[3]}};  // Or or_6, 4 bits wide
  assign or_7_out = 4'b0000 | {1'b0, and_43_out[2], 1'b0, and_43_out[2]} | {2'b00, and_44_out[1], 1'b0} | {and_45_out[3], 2'b00, and_45_out[3]} | {1'b0, and_46_out[2], 2'b00};  // Or or_7, 4 bits wide
  assign or_8_out = {and_47_out[3], 1'b0, {2{and_47_out[3]}}} | {1'b0, {2{and_48_out[2]}}, 1'b0} | {{2{and_49_out[3]}}, 1'b0, and_49_out[3]} | {and_50_out[3], 1'b0, and_50_out[3], 1'b0} | {4{and_51_out[3]}};  // Or or_8, 4 bits wide
  assign or_9_out = or_1_out | or_2_out;  // Or or_9, 4 bits wide
  assign or_10_out = or_3_out | or_4_out;  // Or or_10, 4 bits wide
  assign or_11_out = or_5_out | or_6_out;  // Or or_11, 4 bits wide
  assign or_12_out = or_7_out | or_8_out;  // Or or_12, 4 bits wide
  assign Output = or_9_out | or_10_out | or_11_out | or_12_out;  // Or or_13, 4 bits wide

  // Other names for the same wires on the sheet: a = In[0]; b = In[1]; c = In[2]; d = In[3]; s1 = Selector[0];
  //   s2 = Selector[1]
endmodule
